# Fritzing sketch LCD with KeyPad on Arduino UNO (saved by Fritzing 0.9.2b)

parts:
  Parte1 = Arduino Uno (Rev3)
  Matrix_keypad1 = KEYPAD 4x4
  U1 = LCD-16X2 [package=lcd-16x2]
  R1 = Resistor [tolerance=±5% resistance=220 package="1206 [SMD]"]

nets:
  N1: Parte1.A0, Matrix_keypad1.row3
  N2: Parte1.A1, Matrix_keypad1.row4
  N3: Parte1.D8, Matrix_keypad1.col1
  N4: Parte1.D9_PWM, Matrix_keypad1.col2
  N5: Parte1.D10_PWM/SS, Matrix_keypad1.col3
  N6: Parte1.D11_PWM/MOSI, Matrix_keypad1.col4
  N7: Parte1.D12/MISO, Matrix_keypad1.row1
  N8: Parte1.D13/SCK, Matrix_keypad1.row2
  N9: Parte1.D2, U1.DB7
  N10: Parte1.D3_PWM, U1.DB6
  N11: Parte1.D4, U1.DB5
  N12: Parte1.D5_PWM, U1.DB4
  N13: Parte1.D6_PWM, U1.E
  N14: Parte1.D7, U1.RS
  5V: Parte1.5V, U1.VDD, R1.Pin_0
  GND: Parte1.GND, U1.VSS, U1.VO, U1.R_W, U1.K
  N15: U1.A, R1.Pin_1

notes:
  danielriveraayala@gmail.com

custom parts:
  KEYPAD 4x4: Matrix keypad 16 buttons, 4 rows x 4 columns

// code stored in the sketch: LCD_KEYPAD_ARDUINO_UNO.ino
#include <LiquidCrystal.h>
#include <Keypad.h>

const byte filasKeypad = 4;
const byte columnasKeypad = 4;
char keys[filasKeypad][columnasKeypad] = {
  {'1', '2', '3', 'A'},
  {'4', '5', '6', 'B'},
  {'7', '8', '9', 'C'},
  {'*', '0', '#', 'D'}
  };

char Data[16];
byte data_count = 0;
byte filasPinsKeypad[filasKeypad] = {8, 9, 10, 11};
byte columnasPinsKeypad[columnasKeypad] = {12, 13, 14, 15}; //el pin 14 y 15 corresponden a los Analog In A0 y A1 respectivamente que tambien se pueden utilizar como Digital In

Keypad keypad = Keypad( makeKeymap(keys), filasPinsKeypad, columnasPinsKeypad, filasKeypad, columnasKeypad );
LiquidCrystal lcd(7, 6, 5, 4, 3, 2);


void setup() {
lcd.begin(16, 2);
lcd.print("Teclea algo...");
}

void loop() {
char key = keypad.getKey();
if(data_count>16){
data_count = 0;
}
if(key){
Data[data_count] = key;
lcd.setCursor(data_count, 1);
lcd.print(Data[data_count]);
data_count++;
}
}
