# Fritzing sketch Proyecto Final (saved by Fritzing 0.9.3b)
breadboards: 2

parts:
  GY1 = MPU-6050 Board GY-521 [form="♀ (female)" package=THT]
  Keypad4x1 = Keypad Membran 4x4
  Part1 = Arduino Uno (Rev3)
  J1 = Basic Servo
  o1 = Module display OLED I2C 128x64 SSD1306 [package=THT]
  o2 = Module display OLED I2C 128x64 SSD1306 [package=THT]
  J2 = Basic Servo
  Part2 = Bluetooth HC-06
  Part3 = Tiny RTC - DS1307 Breakout Board
  J3 = Piezo Speaker
  SW1 = DIP Switch 8 Position [package=dipswitch-08]
  R1 = Resistor [tolerance=±5% resistance=220 package="0603 [SMD]"]
  VCC1 = Battery block 9V

nets:
  VCC: GY1.pin1, J1.vcc, o1.VCC, o2.VCC, J2.vcc, Part2.VCC, Part3.VCC, SW1.16, VCC1.+
  GND: GY1.pin2, J1.gnd, o1.GND, o2.GND, J2.gnd, Part2.GND, Part3.GND, J3.pin1, R1.Pin_0, VCC1.-
  N1: GY1.pin3, Part1.A5/SCL, o1.SCL, o2.SCL, Part3.SCL
  N2: GY1.pin4, Part1.A4/SDA, o1.SDA, Part3.SDA
  N3: GY1.pin8, Part1.D2
  N4: Keypad4x1.Pin1, Part1.D12/MISO
  N5: Keypad4x1.Pin2, Part1.D11_PWM/MOSI
  N6: Keypad4x1.Pin5, Part1.D10_PWM/SS
  N7: Keypad4x1.Pin6, Part1.D9_PWM
  N8: Keypad4x1.Pin7, Part1.D8
  N9: Keypad4x1.Pin8, Part1.D7
  N10: Part1.D13/SCK, J3.pin2
  N11: Part1.D0/RX, Part2.TXD
  N12: Part1.D1/TX, Part2.RXD
  N13: Part1.D4, SW1.1, R1.Pin_1
  N14: Part1.D5_PWM, J1.pulse, J2.pulse

custom parts:
  MPU-6050 Board GY-521: Acelerometro y Giroscopio MPU-6050 Board GY-521
  Keypad Membran 4x4: Membrane Keypad 4x4 Matrix
  Module display OLED I2C 128x64 SSD1306: Ecran OLED I2C SSD163 de 128x64 avec connexion I2C
  Tiny RTC - DS1307 Breakout Board: The Tiny RTC is a breakout board for the Dallas Semiconductor/Maxim Integrated DS1307 real-time clock. The DS1307 counts seconds, minutes, hours, date of the month, month, day of the week, and year (with compensation for leap-years). The breakout board also has space for a DS18B20 digital thermometer.
